// Logisim project DLD.circ as structural Verilog: 9 circuits, main circuit 2x1Multiplexer
module _2x1Multiplexer (
  input  I1,
  input  A,
  input  I2,
  output out_4
);

  wire nand_1_out, nand_2_out, nand_3_out;

  nand nand_1 (nand_1_out, A, A);
  nand nand_2 (nand_2_out, I1, nand_1_out);
  nand nand_3 (nand_3_out, A, I2);
  nand nand_4 (out_4, nand_2_out, nand_3_out);
endmodule

module _4x1Multiplexer (
  input  in_1,
  input  in_2,
  input  in_3,
  input  in_4,
  output out_5
);

  wire n2x1multiplexer_1_out_4, n2x1multiplexer_2_out_4;

  _2x1Multiplexer u_2x1multiplexer_1 (.I1(in_1), .I2(in_2), .out_4(n2x1multiplexer_1_out_4));  // open: A
  _2x1Multiplexer u_2x1multiplexer_2 (.I1(in_3), .I2(in_4), .out_4(n2x1multiplexer_2_out_4));  // open: A
  _2x1Multiplexer u_2x1multiplexer_3 (
    .I1(n2x1multiplexer_1_out_4), .I2(n2x1multiplexer_2_out_4), .out_4(out_5));  // open: A
endmodule

module HalfAdder (
  input  A,
  input  B,
  output Carry,
  output Sum
);

  and and_1 (Carry, A, B);
  xor xor_1 (Sum, A, B);
endmodule

module Full_adder (
  input  A,
  input  B,
  input  Cin,
  output Cout,
  output Sum
);

  wire and_1_out, and_2_out, xor_1_out;

  and and_1 (and_1_out, A, B);
  xor xor_1 (xor_1_out, A, B);
  and and_2 (and_2_out, Cin, xor_1_out);
  xor xor_2 (Sum, xor_1_out, Cin);
  or or_1 (Cout, and_1_out, and_2_out);

  // Notes on the sheet:
  //   FullAdder
endmodule

module _1_bit_comparator (
  input  A,
  input  B,
  output A_B,
  output A_B_2,
  output A_B_3
);

  wire not_1_out, not_2_out;

  not not_1 (not_1_out, B);
  not not_2 (not_2_out, A);
  and and_1 (A_B, A, not_1_out);
  and and_2 (A_B_3, not_2_out, B);
  xor xor_1 (A_B_2, A, B);

  // Notes on the sheet:
  //   Comparator
  //   same pr 0,diff pr 1
endmodule

module SR_Latch (
  input  R,
  input  S,
  output Q,
  output out_4
);

  nor nor_1 (Q, R, out_4);
  nor nor_2 (out_4, Q, S);

  // Notes on the sheet:
  //   Q
endmodule

module _2_bit_asynchronous_counter (
  output A,
  output B,
  output A_2,
  output B_2
);

  wire clock_1_out, clock_2_out, d_ff_1_qn, d_ff_2_qn, d_ff_3_qn, d_ff_4_qn, not_1_out;

  Clock clock_1 (.out(clock_1_out));
  not not_1 (not_1_out, clock_1_out);
  D_Flip_Flop #(.trigger("falling")) d_ff_1 (
    .clk(not_1_out), .D(d_ff_1_qn), .Q(A), .Qn(d_ff_1_qn));  // open: preset, en, reset
  D_Flip_Flop #(.trigger("falling")) d_ff_2 (
    .clk(d_ff_1_qn), .D(d_ff_2_qn), .Q(B), .Qn(d_ff_2_qn));  // open: preset, en, reset
  Clock clock_2 (.out(clock_2_out));
  D_Flip_Flop d_ff_3 (.clk(clock_2_out), .D(d_ff_3_qn), .Q(B_2), .Qn(d_ff_3_qn));  // open: preset, en, reset
  D_Flip_Flop d_ff_4 (.clk(d_ff_3_qn), .D(d_ff_4_qn), .Q(A_2), .Qn(d_ff_4_qn));  // open: preset, en, reset

  // Notes on the sheet:
  //   CLK
  //   CLK
endmodule

module _3_bit_asynchronous_counter (
  output out_1,
  output out_2,
  output out_3
);

  wire clock_1_out, d_ff_1_qn, d_ff_2_qn, d_ff_3_qn, not_1_out;

  Clock clock_1 (.out(clock_1_out));
  not not_1 (not_1_out, clock_1_out);
  D_Flip_Flop d_ff_1 (.clk(not_1_out), .D(d_ff_1_qn), .Q(out_3), .Qn(d_ff_1_qn));  // open: preset, en, reset
  D_Flip_Flop d_ff_2 (.clk(d_ff_1_qn), .D(d_ff_2_qn), .Q(out_2), .Qn(d_ff_2_qn));  // open: preset, en, reset
  D_Flip_Flop d_ff_3 (.clk(d_ff_2_qn), .D(d_ff_3_qn), .Q(out_1), .Qn(d_ff_3_qn));  // open: preset, en, reset

  // Notes on the sheet:
  //   CLK
endmodule

module _2_bit_synchronous_counter (
  output out_1,
  output out_2
);

  wire clock_1_out, d_ff_1_qn, d_ff_2_qn, not_1_out, xor_1_out;

  Clock clock_1 (.out(clock_1_out));
  not not_1 (not_1_out, clock_1_out);
  D_Flip_Flop d_ff_1 (.clk(not_1_out), .D(d_ff_1_qn), .Q(out_2), .Qn(d_ff_1_qn));  // open: preset, en, reset
  D_Flip_Flop d_ff_2 (.clk(not_1_out), .D(xor_1_out), .Q(out_1), .Qn(d_ff_2_qn));  // open: preset, en, reset
  xor xor_1 (xor_1_out, d_ff_1_qn, d_ff_2_qn);
endmodule
