// Logisim project gates.circ as structural Verilog: 1 circuit, main circuit main
module main (
  input  in_1,
  input  in_2,
  input  in_3,
  input  in_4,
  input  in_5,
  output out_6,
  output out_7,
  output out_8
);

  wire transistor_3_out, transistor_7_out;

  Transistor transistor_1 (.in(1'b1), .out(out_7), .gate(in_2));
  Transistor #(.\type ("n")) transistor_2 (.in(1'b0), .out(out_7), .gate(in_2));
  Transistor #(.\type ("n")) transistor_3 (.in(1'b1), .out(transistor_3_out), .gate(in_1));
  Transistor #(.\type ("n")) transistor_4 (.in(transistor_3_out), .out(out_6), .gate(in_4));
  Transistor transistor_5 (.in(1'b0), .out(out_6), .gate(in_1));
  Transistor transistor_6 (.in(1'b0), .out(out_6), .gate(in_4));
  Transistor #(.\type ("n")) transistor_7 (.in(1'b0), .out(transistor_7_out), .gate(in_3));
  Transistor #(.\type ("n")) transistor_8 (.in(transistor_7_out), .out(out_8), .gate(in_5));
  Transistor transistor_9 (.in(1'b1), .out(out_8), .gate(in_5));
  Transistor transistor_10 (.in(1'b1), .out(out_8), .gate(in_3));

  // Notes on the sheet:
  //   make all transistors direction towards output
endmodule
